# Fritzing sketch esquemaCircuito (saved by Fritzing 0.9.3b)
breadboards: 1

parts:
  Componente1 = Arduino Uno (Rev3)
  LED2 = LED - 5mm [color="Yellow (585nm)" package="5 mm [THT]"]
  LED3 = LED - 5mm [color="Green (555nm)" package="5 mm [THT]"]
  R1 = Resistor [tolerance=±5% resistance=220 package=THT]
  LED4 = LED - 5mm [color="Red (633nm)" package="5 mm [THT]"]
  LED5 = LED - 5mm [color="Yellow (585nm)" package="5 mm [THT]"]
  LED6 = LED - 5mm [color="Green (555nm)" package="5 mm [THT]"]
  R2 = Resistor [tolerance=±5% resistance=220 package=THT]
  hc-sr1 = hc-sr04
  LED1 = LED - 5mm [color="Red (633nm)" package="5 mm [THT]"]

nets (from the schematic view):
  N1: Componente1.D8, LED3.anode
  N2: Componente1.D9_PWM, LED2.anode
  N3: Componente1.D10_PWM/SS, LED1.anode
  N4: Componente1.D11_PWM/MOSI, LED6.anode
  N5: Componente1.D12/MISO, LED5.anode
  N6: Componente1.D13/SCK, LED4.anode
  N7: Componente1.D4, Componente1.5V, hc-sr1.Trig
  N8: Componente1.D5_PWM, hc-sr1.Echo
  GND: Componente1.GND, R1.Pin_1, R2.Pin_1, hc-sr1.GND
  N9: LED2.cathode, LED3.cathode, R1.Pin_0, LED1.cathode
  N10: LED4.cathode, LED5.cathode, LED6.cathode, R2.Pin_0
